# Fritzing sketch bbq schematic v1 (saved by Fritzing 0.9.0b)
circuit board: 8.46667cm x 5.64444cm
breadboards: 1

parts:
  U1 = NodeMCU V1.0
  OLED_I2C1 = OLED 128x64 I2C Monochrome Display
  R1 = Resistor [tolerance=±5% resistance=10k package=THT]
  U2 = 2.5mm Audio Jack [package=stereojack2.5mm_stereojack2.5mm]

nets:
  N1: U1.D3, OLED_I2C1.SDA
  N2: U1.3V3, R1.Pin_0
  GND: U1.GND, OLED_I2C1.GND, U2.SLEEVE
  N3: U1.D5, OLED_I2C1.SCK
  VIN: U1.Vin, OLED_I2C1.VDD
  N4: U1.A0, R1.Pin_1, U2.LEFT

custom parts:
  NodeMCU V1.0: ESP8266 based NodeMCU
